// Logisim project entireProcessor.circ as structural Verilog: 17 circuits, main circuit main
module main (
  output [31:0] eax,
  output [31:0] data,
  output [15:0] addr,
  output [31:0] ecx,
  output [31:0] valA,
  output [31:0] edx,
  output [31:0] valE,
  output [31:0] valB,
  output [31:0] valM,
  output [31:0] ebx,
  output [15:0] Val_P,
  output [3:0] Ra,
  output [3:0] icode,
  output [31:0] esi,
  output [3:0] Rb,
  output [31:0] valc,
  output [3:0] ifun,
  output [3:0] srcA,
  output [3:0] srcB,
  output [31:0] edi,
  output [3:0] dstE,
  output [15:0] current_pc,
  output [3:0] dstM,
  output [31:0] esp,
  output [15:0] new_pc,
  output [31:0] ebp
);

  wire clock_1_out, fetch_unit_1_r, fetch_unit_1_v, main_1_p4, mem_control_1_p2, mem_control_1_p3;

  Clock clock_1 (.out(clock_1_out));
  PC pc_1 (.Clock(clock_1_out), .Output_PC(current_pc), .Input_PC(new_pc));
  // MEM__CONTROL mem_control_1: pin names not known; wires that end beside it: icode, mem_control_1_p2, mem_control_1_p3, mem_control_1_p2, mem_control_1_p3
  Register register_1 (
    .destE(dstE), .ValE(valE), .destM(dstM), .ValM(valM), .clock(clock_1_out), .valA(data), .srcA(srcA),
    .srcB(srcB), .valB(valB), .eax(eax), .ecx(ecx), .edx(edx), .ebx(ebx), .esi(esi), .edi(edi), .esp(esp),
    .ebp(ebp));
  dstE dste_1 (.cnd(main_1_p4), .rB(Rb), .icode(icode), .out_4(dstE));
  Fetch_Unit fetch_unit_1 (
    .PC_Input(current_pc), .R(fetch_unit_1_r), .V(fetch_unit_1_v), .icode(icode), .ifun(ifun), .ra(Ra),
    .rb(Rb), .valc(valc), .clock(clock_1_out));
  // DATA_MEMORY data_memory_1: pin names not known; wires that end beside it: valM, clock_1_out, data
  // ADDR addr_1: pin names not known; wires that end beside it: valE, addr, addr, data, icode
  // final_Execution_Unit_main main_1: pin names not known; wires that end beside it: clock_1_out, ifun, icode, main_1_p4, valc, valE, data, valB
  srcA srca_1 (.rA(Ra), .icode(icode), .out_3(srcA));
  dstM dstm_1 (.rA(Ra), .icode(icode), .out_3(dstM));
  PC_Increment pc_increment_1 (.OLD_PC(current_pc), .NEW_PC(Val_P), .V(fetch_unit_1_v), .R(fetch_unit_1_r));
  NEW_PC new_pc_1 (.icode(icode), .PC_Code(Val_P), .New_PC(new_pc), .Val_M(valM), .Cnd(main_1_p4));
  srcB srcb_1 (.rB(Rb), .icode(icode), .out_3(srcB));

  assign valA = data;
endmodule

module PC_Increment (
  input  [15:0] OLD_PC,
  input  V,
  input  R,
  output [15:0] NEW_PC
);

  wire [15:0] adder_1_out, adder_2_out, adder_3_out, adder_4_out;

  Adder #(.width(16)) adder_1 (.a(OLD_PC), .b(16'h1), .out(adder_1_out));  // open: cin, cout
  Adder #(.width(16)) adder_2 (.a(OLD_PC), .b(16'h2), .out(adder_2_out));  // open: cin, cout
  Adder #(.width(16)) adder_3 (.a(OLD_PC), .b(16'h5), .out(adder_3_out));  // open: cin, cout
  Adder #(.width(16)) adder_4 (.a(OLD_PC), .b(16'h6), .out(adder_4_out));  // open: cin, cout
  Multiplexer #(.select(2), .width(16)) multiplexer_1 (
    .in0(adder_1_out), .in1(adder_2_out), .in2(adder_3_out), .in3(adder_4_out), .out(NEW_PC), .sel({V, R}));  // open: en
endmodule

module Fetch_Unit (
  input  [15:0] PC_Input,
  input  clock,
  output [3:0] icode,
  output [3:0] ifun,
  output [3:0] ra,
  output [3:0] rb,
  output [31:0] valc,
  output R,
  output V
);

  wire control_box_1_e0, control_box_1_e1, control_box_1_e2, control_box_1_e3, control_box_1_e4,
       control_box_1_e5;
  wire [7:0] ram_1_data;
  wire [15:0] control_box_1_pc_output;

  split split_1 (._8_bit_input(ram_1_data), .e0(control_box_1_e0), .clock(clock), .ifun(ifun), .icode(icode));
  control_box control_box_1 (
    .PC_Input(PC_Input), .Clock(clock), .I(V), .R(R), .e0(control_box_1_e0), .e1(control_box_1_e1),
    .e2(control_box_1_e2), .e3(control_box_1_e3), .e4(control_box_1_e4), .e5(control_box_1_e5),
    .PC_Output(control_box_1_pc_output));
  align align_1 (
    ._8_bit_input(ram_1_data), .e2(control_box_1_e1), .e3(control_box_1_e2), .e4(control_box_1_e3),
    .e5(control_box_1_e4), .e6(control_box_1_e5), .clock(clock), .reg_B(rb), .reg_A(ra), .valc(valc));
  RV_Control rv_control_1 (.in_1(icode[0]), .in_2(icode[1]), .in_3(icode[2]), .in_4(icode[3]), .needsR(R), .needsV(V));
  RAM #(.addrWidth(16)) ram_1 (.addr(control_box_1_pc_output), .data(ram_1_data), .clk(clock));  // open: sel, ld, clr

  // Notes on the sheet:
  //   RV CONTROL
endmodule

module align (
  input  [7:0] _8_bit_input,
  input  e2,
  input  e3,
  input  e4,
  input  e5,
  input  e6,
  input  clock,
  output [3:0] reg_B,
  output [3:0] reg_A,
  output [31:0] valc
);

  Register_part #(.width(4)) register_1 (.D(_8_bit_input[3:0]), .en(e2), .Q(reg_B), .clk(clock));  // open: clr
  Register_part #(.width(4)) register_2 (.D(_8_bit_input[7:4]), .en(e2), .Q(reg_A), .clk(clock));  // open: clr
  Register_part #(.width(4)) register_3 (.D(_8_bit_input[3:0]), .en(e3), .Q(valc[27:24]), .clk(clock));  // open: clr
  Register_part #(.width(4)) register_4 (.D(_8_bit_input[7:4]), .en(e3), .Q(valc[31:28]), .clk(clock));  // open: clr
  Register_part #(.width(4)) register_5 (.D(_8_bit_input[3:0]), .en(e4), .Q(valc[19:16]), .clk(clock));  // open: clr
  Register_part #(.width(4)) register_6 (.D(_8_bit_input[7:4]), .en(e4), .Q(valc[23:20]), .clk(clock));  // open: clr
  Register_part #(.width(4)) register_7 (.D(_8_bit_input[3:0]), .en(e5), .Q(valc[11:8]), .clk(clock));  // open: clr
  Register_part #(.width(4)) register_8 (.D(_8_bit_input[7:4]), .en(e5), .Q(valc[15:12]), .clk(clock));  // open: clr
  Register_part #(.width(4)) register_9 (.D(_8_bit_input[3:0]), .en(e6), .Q(valc[3:0]), .clk(clock));  // open: clr
  Register_part #(.width(4)) register_10 (.D(_8_bit_input[7:4]), .en(e6), .Q(valc[7:4]), .clk(clock));  // open: clr
endmodule

module split (
  input  [7:0] _8_bit_input,
  input  e0,
  input  clock,
  output [3:0] ifun,
  output [3:0] icode
);

  Register_part #(.width(4)) register_1 (.D(_8_bit_input[3:0]), .en(e0), .Q(ifun), .clk(clock));  // open: clr
  Register_part #(.width(4)) register_2 (.D(_8_bit_input[7:4]), .en(e0), .Q(icode), .clk(clock));  // open: clr
endmodule

module control_box (
  input  [15:0] PC_Input,
  input  Clock,
  input  I,
  input  R,
  output e0,
  output e1,
  output e2,
  output e3,
  output e4,
  output e5,
  output [15:0] PC_Output
);

  wire and_7_out, and_8_out, not_1_out, or_1_out;
  wire [3:0] counter_1_q;
  wire [15:0] adder_1_out, controlled_buffer_1_out;

  assign controlled_buffer_1_out = and_7_out ? PC_Input : 16'bz;  // Controlled_Buffer controlled_buffer_1
  Counter #(.width(4), .max('h9)) counter_1 (.Q(counter_1_q), .clk(Clock));  // open: load, D, count, carry, clr
  Register_part #(.width(16)) register_1 (
    .D(controlled_buffer_1_out), .Q(PC_Output), .clk(and_8_out));  // open: en, clr
  not not_1 (not_1_out, and_7_out);
  assign controlled_buffer_1_out = not_1_out ? adder_1_out : 16'bz;  // Controlled_Buffer controlled_buffer_2
  and and_1 (e0, ~counter_1_q[0], ~counter_1_q[1], ~counter_1_q[2], ~counter_1_q[3]);  // AND_Gate
  and and_2 (e1, ~counter_1_q[1], ~counter_1_q[3], ~counter_1_q[2], R, counter_1_q[0]);  // AND_Gate
  and and_3 (e2, ~counter_1_q[3], ~counter_1_q[2], counter_1_q[1], ~counter_1_q[0], I);  // AND_Gate
  and and_4 (e3, I, counter_1_q[1], ~counter_1_q[2], ~counter_1_q[3], counter_1_q[0]);  // AND_Gate
  and and_5 (e4, counter_1_q[2], ~counter_1_q[3], ~counter_1_q[1], ~counter_1_q[0], I);  // AND_Gate
  and and_6 (e5, I, counter_1_q[0], ~counter_1_q[1], ~counter_1_q[3], counter_1_q[2]);  // AND_Gate
  and and_7 (and_7_out, counter_1_q[0], ~counter_1_q[1], ~counter_1_q[2], counter_1_q[3]);  // AND_Gate
  Adder #(.width(16)) adder_1 (.a(PC_Output), .b(16'h1), .out(adder_1_out));  // open: cin, cout
  or or_1 (or_1_out, e0, e1, e2, and_7_out, e3, e4, e5);
  and and_8 (and_8_out, or_1_out, Clock);
endmodule

module RV_Control (
  input  in_1,
  input  in_2,
  input  in_3,
  input  in_4,
  output needsR,
  output needsV
);

  wire add_out, halt_out, irrmov_out, jmp_out, jz_out, ld_out, mul_out, rrmov_out, st_out;

  and irrmov (irrmov_out, ~in_1, ~in_2, ~in_3, ~in_4);  // AND_Gate
  and rrmov (rrmov_out, in_1, ~in_2, ~in_3, ~in_4);  // AND_Gate
  and ld (ld_out, in_2, ~in_1, ~in_3, ~in_4);  // AND_Gate
  and st (st_out, in_2, in_1, ~in_4, ~in_3);  // AND_Gate
  and add (add_out, ~in_1, ~in_2, in_3, ~in_4);  // AND_Gate
  and mul (mul_out, in_1, ~in_2, in_3, ~in_4);  // AND_Gate
  and jmp (jmp_out, ~in_1, in_2, in_3, ~in_4);  // AND_Gate
  and jz (jz_out, ~in_4, in_1, in_2, in_3);  // AND_Gate
  and halt (halt_out, ~in_1, ~in_2, ~in_3, in_4);  // AND_Gate
  or or_1 (needsR, irrmov_out, add_out, rrmov_out, st_out, ld_out, mul_out);
  or or_2 (needsV, st_out, ld_out, jmp_out, jz_out, irrmov_out);
endmodule

module NEW_PC (
  input  [3:0] icode,
  input  Cnd,
  input  [15:0] PC_Code,
  input  [31:0] Val_M,
  output [15:0] New_PC
);

  wire halt_out, jmp_out, jz_out, not_1_out, or_1_out;
  wire [15:0] multiplexer_1_out;

  and halt (halt_out, ~icode[0], ~icode[1], ~icode[2], icode[3]);  // AND_Gate
  and jz (jz_out, icode[0], icode[1], icode[2], ~icode[3], Cnd);  // AND_Gate
  and jmp (jmp_out, ~icode[0], icode[1], icode[2], ~icode[3]);  // AND_Gate
  Multiplexer #(.width(16)) multiplexer_1 (
    .in0(PC_Code), .in1(Val_M[15:0]), .out(multiplexer_1_out), .sel(or_1_out));  // open: en
  or or_1 (or_1_out, jmp_out, jz_out);
  not not_1 (not_1_out, halt_out);
  assign New_PC = not_1_out ? multiplexer_1_out : 16'bz;  // Controlled_Buffer controlled_buffer_1
endmodule

module PC (
  input  Clock,
  input  [15:0] Input_PC,
  output [15:0] Output_PC
);

  wire and_1_out;
  wire [3:0] counter_1_q;
  wire [15:0] controlled_buffer_1_out;

  Counter #(.width(4), .max('h9)) counter_1 (.Q(counter_1_q), .clk(Clock));  // open: load, D, count, carry, clr
  and and_1 (and_1_out, ~counter_1_q[0], ~counter_1_q[1], ~counter_1_q[2], counter_1_q[3]);  // AND_Gate
  assign controlled_buffer_1_out = and_1_out ? Input_PC : 16'bz;  // Controlled_Buffer controlled_buffer_1
  Register_part #(.width(16)) register_1 (.D(controlled_buffer_1_out), .Q(Output_PC), .clk(Clock));  // open: en, clr
endmodule

// 2 read 2 write reg
module Register (
  input  [3:0] destE,
  input  [31:0] ValE,
  input  [3:0] destM,
  input  [3:0] srcA,
  input  [31:0] ValM,
  input  [3:0] srcB,
  input  clock,
  output [31:0] eax,
  output [31:0] ecx,
  output [31:0] edx,
  output [31:0] ebx,
  output [31:0] esi,
  output [31:0] edi,
  output [31:0] esp,
  output [31:0] ebp,
  output [31:0] valA,
  output [31:0] valB
);

  wire decode_1__0, decode_1__8, decode_1_out_3, decode_1_out_4, decode_1_out_5, decode_1_out_6,
       decode_1_out_7, decode_1_out_8, decode_2__0, decode_2__8, decode_2_out_3, decode_2_out_4,
       decode_2_out_5, decode_2_out_6, decode_2_out_7, decode_2_out_8, decode_3__0, decode_3__8,
       decode_3_out_3, decode_3_out_4, decode_3_out_5, decode_3_out_6, decode_3_out_7, decode_3_out_8,
       enable_registers_1_out_3, enable_registers_1_out_4, enable_registers_1_out_5,
       enable_registers_1_out_6, enable_registers_1_out_7, enable_registers_1_out_8,
       enable_registers_1_out_9, enable_registers_1_out_10;
  wire [31:0] multiplexer_1_out, multiplexer_2_out, multiplexer_3_out, multiplexer_4_out, multiplexer_5_out,
       multiplexer_6_out, multiplexer_7_out, multiplexer_8_out;

  enable_registers enable_registers_1 (
    .destM(destM), .destE(destE), .out_3(enable_registers_1_out_3), .out_4(enable_registers_1_out_4),
    .out_5(enable_registers_1_out_5), .out_6(enable_registers_1_out_6), .out_7(enable_registers_1_out_7),
    .out_8(enable_registers_1_out_8), .out_9(enable_registers_1_out_9), .out_10(enable_registers_1_out_10));
  decode decode_1 (
    .in_1(destM), ._0(decode_1__0), .out_3(decode_1_out_3), .out_4(decode_1_out_4), .out_5(decode_1_out_5),
    .out_6(decode_1_out_6), .out_7(decode_1_out_7), .out_8(decode_1_out_8), ._8(decode_1__8));
  Multiplexer #(.width(32)) multiplexer_1 (
    .in0(ValE), .in1(ValM), .out(multiplexer_1_out), .sel(decode_1__0));  // open: en
  Multiplexer #(.width(32)) multiplexer_2 (
    .in0(ValE), .in1(ValM), .out(multiplexer_2_out), .sel(decode_1_out_3));  // open: en
  Multiplexer #(.width(32)) multiplexer_3 (
    .in0(ValE), .in1(ValM), .out(multiplexer_3_out), .sel(decode_1_out_4));  // open: en
  Multiplexer #(.width(32)) multiplexer_4 (
    .in0(ValE), .in1(ValM), .out(multiplexer_4_out), .sel(decode_1_out_5));  // open: en
  Multiplexer #(.width(32)) multiplexer_5 (
    .in0(ValE), .in1(ValM), .out(multiplexer_5_out), .sel(decode_1_out_6));  // open: en
  Multiplexer #(.width(32)) multiplexer_6 (
    .in0(ValE), .in1(ValM), .out(multiplexer_6_out), .sel(decode_1_out_7));  // open: en
  Multiplexer #(.width(32)) multiplexer_7 (
    .in0(ValE), .in1(ValM), .out(multiplexer_7_out), .sel(decode_1_out_8));  // open: en
  Multiplexer #(.width(32)) multiplexer_8 (
    .in0(ValE), .in1(ValM), .out(multiplexer_8_out), .sel(decode_1__8));  // open: en
  Register_part #(.width(32)) register_1 (
    .D(multiplexer_1_out), .en(enable_registers_1_out_3), .Q(eax), .clk(clock));  // open: clr
  Register_part #(.width(32)) register_2 (
    .D(multiplexer_2_out), .en(enable_registers_1_out_4), .Q(ecx), .clk(clock));  // open: clr
  Register_part #(.width(32)) register_3 (
    .D(multiplexer_3_out), .en(enable_registers_1_out_5), .Q(edx), .clk(clock));  // open: clr
  Register_part #(.width(32)) register_4 (
    .D(multiplexer_4_out), .en(enable_registers_1_out_6), .Q(ebx), .clk(clock));  // open: clr
  Register_part #(.width(32)) register_5 (
    .D(multiplexer_5_out), .en(enable_registers_1_out_7), .Q(esi), .clk(clock));  // open: clr
  Register_part #(.width(32)) register_6 (
    .D(multiplexer_6_out), .en(enable_registers_1_out_8), .Q(edi), .clk(clock));  // open: clr
  Register_part #(.width(32)) register_7 (
    .D(multiplexer_7_out), .en(enable_registers_1_out_9), .Q(esp), .clk(clock));  // open: clr
  Register_part #(.width(32)) register_8 (
    .D(multiplexer_8_out), .en(enable_registers_1_out_10), .Q(ebp), .clk(clock));  // open: clr
  assign valA = decode_2__0 ? eax : 32'bz;  // Controlled_Buffer controlled_buffer_1
  assign valA = decode_2_out_3 ? ecx : 32'bz;  // Controlled_Buffer controlled_buffer_2
  assign valA = decode_2_out_4 ? edx : 32'bz;  // Controlled_Buffer controlled_buffer_3
  assign valA = decode_2_out_5 ? ebx : 32'bz;  // Controlled_Buffer controlled_buffer_4
  assign valA = decode_2_out_6 ? esi : 32'bz;  // Controlled_Buffer controlled_buffer_5
  assign valA = decode_2_out_7 ? edi : 32'bz;  // Controlled_Buffer controlled_buffer_6
  assign valA = decode_2_out_8 ? esp : 32'bz;  // Controlled_Buffer controlled_buffer_7
  assign valA = decode_2__8 ? ebp : 32'bz;  // Controlled_Buffer controlled_buffer_8
  assign valB = decode_3__0 ? eax : 32'bz;  // Controlled_Buffer controlled_buffer_9
  assign valB = decode_3_out_3 ? ecx : 32'bz;  // Controlled_Buffer controlled_buffer_10
  assign valB = decode_3_out_4 ? edx : 32'bz;  // Controlled_Buffer controlled_buffer_11
  assign valB = decode_3_out_5 ? ebx : 32'bz;  // Controlled_Buffer controlled_buffer_12
  assign valB = decode_3_out_6 ? esi : 32'bz;  // Controlled_Buffer controlled_buffer_13
  Controlled_Buffer #(.width(32)) controlled_buffer_14 (.in(edi), .en(decode_3_out_7));  // open: out
  assign valB = decode_3_out_8 ? esp : 32'bz;  // Controlled_Buffer controlled_buffer_15
  assign valB = decode_3__8 ? ebp : 32'bz;  // Controlled_Buffer controlled_buffer_16
  decode decode_2 (
    .in_1(srcA), ._0(decode_2__0), .out_3(decode_2_out_3), .out_4(decode_2_out_4), .out_5(decode_2_out_5),
    .out_6(decode_2_out_6), .out_7(decode_2_out_7), .out_8(decode_2_out_8), ._8(decode_2__8));
  decode decode_3 (
    .in_1(srcB), ._0(decode_3__0), .out_3(decode_3_out_3), .out_4(decode_3_out_4), .out_5(decode_3_out_5),
    .out_6(decode_3_out_6), .out_7(decode_3_out_7), .out_8(decode_3_out_8), ._8(decode_3__8));
endmodule

module decode (
  input  [3:0] in_1,
  output _0,
  output out_3,
  output out_4,
  output out_5,
  output out_6,
  output out_7,
  output out_8,
  output _8
);

  Decoder #(.select(4)) decoder_1 (
    .out0(_0), .out1(out_3), .out2(out_4), .out3(out_5), .out4(out_6), .out5(out_7), .out6(out_8), .out7(_8),
    .sel(in_1));  // open: out8, out9, out10, out11, out12, out13, out14, out15, en
endmodule

module enable_registers (
  input  [3:0] destM,
  input  [3:0] destE,
  output out_3,
  output out_4,
  output out_5,
  output out_6,
  output out_7,
  output out_8,
  output out_9,
  output out_10
);

  wire decoder_1_out0, decoder_1_out1, decoder_1_out2, decoder_1_out3, decoder_1_out4, decoder_1_out5,
       decoder_1_out6, decoder_1_out7, decoder_1_out8, decoder_2_out0, decoder_2_out1, decoder_2_out2,
       decoder_2_out3, decoder_2_out4, decoder_2_out5, decoder_2_out6, decoder_2_out7, decoder_2_out8;

  Decoder #(.select(4)) decoder_1 (
    .out0(decoder_1_out0), .out1(decoder_1_out1), .out2(decoder_1_out2), .out3(decoder_1_out3),
    .out4(decoder_1_out4), .out5(decoder_1_out5), .out6(decoder_1_out6), .out7(decoder_1_out7),
    .out8(decoder_1_out8), .sel(destM));  // open: out9, out10, out11, out12, out13, out14, out15, en
  Decoder #(.select(4)) decoder_2 (
    .out0(decoder_2_out0), .out1(decoder_2_out1), .out2(decoder_2_out2), .out3(decoder_2_out3),
    .out4(decoder_2_out4), .out5(decoder_2_out5), .out6(decoder_2_out6), .out7(decoder_2_out7),
    .out8(decoder_2_out8), .sel(destE));  // open: out9, out10, out11, out12, out13, out14, out15, en
  or or_1 (out_3, decoder_1_out0, decoder_2_out0);
  or or_2 (out_4, decoder_1_out1, decoder_2_out1, decoder_1_out2, decoder_2_out2);
  or or_3 (out_5, decoder_1_out3, decoder_2_out3);
  or or_4 (out_6, decoder_2_out4, decoder_1_out4);
  or or_5 (out_7, decoder_1_out5, decoder_2_out5);
  or or_6 (out_8, decoder_1_out6, decoder_2_out6);
  or or_7 (out_9, decoder_1_out7, decoder_2_out7);
  or or_8 (out_10, decoder_2_out8, decoder_1_out8);
endmodule

// Register
module whole_register_file (
  input  [31:0] valE,
  input  clock,
  input  [31:0] valM,
  input  CND,
  input  [3:0] rA,
  input  [3:0] icode,
  input  [3:0] rB,
  output [31:0] valA,
  output [31:0] valB
);

  wire [3:0] dste_1_out_4, dstm_1_out_3, srca_1_out_3, srcb_1_out_3;

  Register register_1 (
    .destE(dste_1_out_4), .ValE(valE), .destM(dstm_1_out_3), .ValM(valM), .clock(clock), .valA(valA),
    .srcA(srca_1_out_3), .srcB(srcb_1_out_3), .valB(valB));  // open: eax, ecx, edx, ebx, esi, edi, esp, ebp
  dstE dste_1 (.cnd(CND), .rB(rB), .icode(icode), .out_4(dste_1_out_4));
  srcA srca_1 (.rA(rA), .icode(icode), .out_3(srca_1_out_3));
  dstM dstm_1 (.rA(rA), .icode(icode), .out_3(dstm_1_out_3));
  srcB srcb_1 (.rB(rB), .icode(icode), .out_3(srcb_1_out_3));
endmodule

module srcB (
  input  [3:0] rB,
  input  [3:0] icode,
  output [3:0] out_3
);

  wire and_1_out, and_2_out, or_1_out;

  and and_1 (and_1_out, ~icode[0], ~icode[1], icode[2], ~icode[3]);  // AND_Gate
  and and_2 (and_2_out, icode[0], ~icode[1], icode[2], ~icode[3]);  // AND_Gate
  Multiplexer #(.width(4)) multiplexer_1 (.in0(4'b1111), .in1(rB), .out(out_3), .sel(or_1_out));  // open: en
  or or_1 (or_1_out, and_1_out, and_2_out);
endmodule

module srcA (
  input  [3:0] rA,
  input  [3:0] icode,
  output [3:0] out_3
);

  wire and_1_out, and_2_out, and_3_out, and_4_out, or_1_out;

  Multiplexer #(.width(4)) multiplexer_1 (.in0(4'b1111), .in1(rA), .out(out_3), .sel(or_1_out));  // open: en
  and and_1 (and_1_out, icode[0], ~icode[1], ~icode[2], ~icode[3]);  // AND_Gate
  and and_2 (and_2_out, icode[0], icode[1], ~icode[2], ~icode[3]);  // AND_Gate
  and and_3 (and_3_out, ~icode[0], ~icode[1], icode[2], ~icode[3]);  // AND_Gate
  and and_4 (and_4_out, icode[0], ~icode[1], icode[2], ~icode[3]);  // AND_Gate
  or or_1 (or_1_out, and_1_out, and_2_out, and_3_out, and_4_out);
endmodule

module dstM (
  input  [3:0] rA,
  input  [3:0] icode,
  output [3:0] out_3
);

  wire and_1_out, and_2_out, and_3_out, and_4_out, or_1_out;

  Multiplexer #(.width(4)) multiplexer_1 (.in0(4'b1111), .in1(rA), .out(out_3), .sel(or_1_out));  // open: en
  and and_1 (and_1_out, ~icode[0], ~icode[1], ~icode[2], ~icode[3]);  // AND_Gate
  and and_2 (and_2_out, ~icode[0], icode[1], ~icode[2], ~icode[3]);  // AND_Gate
  and and_3 (and_3_out, ~icode[0], ~icode[1], icode[2], ~icode[3]);  // AND_Gate
  and and_4 (and_4_out, icode[0], ~icode[1], icode[2], ~icode[3]);  // AND_Gate
  or or_1 (or_1_out, and_1_out, and_2_out, and_3_out, and_4_out);
endmodule

module dstE (
  input  [3:0] rB,
  input  [3:0] icode,
  input  cnd,
  output [3:0] out_4
);

  wire and_1_out;

  and and_1 (and_1_out, icode[0], ~icode[1], ~icode[2], ~icode[3], ~cnd);  // AND_Gate
  Multiplexer #(.width(4)) multiplexer_1 (.in0(4'b1111), .in1(rB), .out(out_4), .sel(and_1_out));  // open: en
endmodule
